# Fritzing sketch Potentiometer7SegmentUno12V (saved by Fritzing 0.9.2b)

parts:
  Part3 = Arduino Uno (Rev3) - ICSP
  PART1 = OpenSegment Serial Display - 20mm (Blue) [part_number=COM-11647]
  Part4 = Digital Temperature Sensor Breakout - TMP102
  part = Battery block 9V

nets (from the breadboard view):
  N1: Part3.A4/SDA, Part4.SDA
  N2: Part3.A5/SCL, Part4.SCL
  N3: Part3.D10_PWM/SS, PART1.SS
  N4: Part3.D11_PWM/MOSI, PART1.SDI
  N5: Part3.D12/MISO, PART1.SDO
  N6: Part3.D13/SCK, PART1.SCK
  GND: Part3.GND, PART1.GND, Part4.GND, Part4.ADD0, part.-
  N7: Part3.3V3, Part4.V+
  5V: Part3.5V, PART1.VCC
  N8: Part3.VIN, part.+

custom parts:
  OpenSegment Serial Display - 20mm (Blue): OpenSegment makes it easy to add a large 7-segment display to your project. Because larger 7-segment displays pull more power than a microcontroller is able to drive directly, the OpenSegment has 8 PNP and 4 NPN transistors in order to drive the segments at their maximum brightness! The on-board ATmega328 receives data over multiple digital interfaces (such as TWI, UART and SPI) and does all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
